# Fritzing sketch Arduplane (saved by Fritzing 0.9.2b)

parts:
  Arduino_UNO = Arduino Uno (Rev3)
  Arduino_Nano = Arduino Nano (Rev3.0)
  Tx = mystery part, 3 pins [chip_label=?]
  Rx = mystery part, 4 pins [chip_label=?]
  J1 = Basic Servo  # not connected
  J4 = Basic Servo
  Part1 = Thumb Joystick
  U1 = POT [package=pot_alpha_rv16af-20]

nets:
  N1: Arduino_UNO.A0, U1.S
  N2: Arduino_UNO.A1, Part1.VERT
  N3: Arduino_UNO.A2, Part1.HORZ
  N4: Arduino_UNO.D12/MISO, Tx.pin1
  5V: Arduino_UNO.5V, Tx.pin2, Part1.VCC
  GND: Arduino_UNO.GND, Tx.pin3, Part1.GND
  N5: Arduino_Nano.D11/MOSI, Rx.pin3
  GND_2: Arduino_Nano.GND, Rx.pin4, J4.gnd
  5V_2: Arduino_Nano.5V, Rx.pin1, J4.vcc

notes:
  Transmitter
  Reciever
  Ailrons
  ESC
  Brushless
  DC motor
